# Fritzing sketch Схема (saved by Fritzing 0.9.3b)
circuit board: 13.8395cm x 7.10099cm
breadboards: 1

parts:
  Часть2 = Real Time Clock Module - DS1307 RTC Breakout Board
  J2 = Basic Servo
  U4 = ESP8266 NodeMCU LoLin module
  J6 = Screw terminal - 2 pins [package=THT]
  Часть4 = Soil Moisture Sensor
  Часть6 = Adafruit ADS1115 16Bit I2C ADC [part_number="Adafruit #1085"]
  S1 = Round Pushbutton
  S2 = Round Pushbutton
  S3 = Round Pushbutton
  S4 = Round Pushbutton
  S5 = Round Pushbutton
  J8 = Camdenboss CTB0158-3 [part_number=CTB0158-3 package=THT]
  J9 = Camdenboss CTB0158-3 [part_number=CTB0158-3 package=THT]
  J11 = Camdenboss CTB0158-4 [part_number=CTB0158-4 package=THT]
  J13 = Camdenboss CTB0158-5 [part_number=CTB0158-5 package=THT]
  R2 = Resistor [tolerance=±5% resistance=220 package=THT]
  R3 = Resistor [tolerance=±5% resistance=220 package=THT]
  J1 = Basic Servo
  Часть3 = BME280 Breakout
  R9 = Resistor [tolerance=±5% resistance=220 package=THT]
  R8 = Resistor [tolerance=±5% resistance=220 package=THT]
  R6 = Resistor [tolerance=±5% resistance=220 package=THT]
  R7 = Resistor [tolerance=±5% resistance=220 package=THT]
  R5 = Resistor [tolerance=±5% resistance=220 package=THT]
  J14 = Camdenboss CTB0158-2 [part_number=CTB0158-2 package=THT]
  J4 = Screw terminal - 2 pins [package=THT]
  LCD1 = LCD screen
  U2 = RELAY-SOLIDSTATE [package=relay-s108t02]
  J10 = Camdenboss CTB0158-4 [part_number=CTB0158-4 package=THT]
  J3 = Screw terminal - 2 pins [package=THT]
  U3 = RELAY-SOLIDSTATE [package=relay-s108t02]
  LCM1602_IIC1 = LCM1602 IIC [part_number="LCM1602 IIC" chip_label="LCM1602 IIC" package="DIP (Dual Inline) [THT]"]
  J12 = Camdenboss CTB0158-5 [part_number=CTB0158-5 package=THT]
  J7 = Screw terminal - 2 pins [package=THT]
  J5 = Screw terminal - 2 pins [package=THT]
  U1 = RELAY-SOLIDSTATE [package=relay-s108t02]
  U5 = RELAY-SOLIDSTATE [package=relay-s108t02]

nets:
  5V: Часть2.5V, J2.vcc, U4.Vin, Часть4.VCC, Часть6.VDD, J8.pin1, J11.pin3, R3.Pin_1, J1.vcc, Часть3.3.3V, J14.pin1
  GND: Часть2.GND, J2.gnd, U4.GND, J6.pin1, Часть4.GND, Часть6.GND, J8.pin3, J11.pin4, J13.pin5, J1.gnd, Часть3.GND, J14.pin2
  N1: Часть2.SCL, U4.D1, Часть6.SCL, J11.pin1, Часть3.SCK/SCL
  N2: Часть2.SDA, U4.D2, Часть6.SDA, J11.pin2, Часть3.SDI/SDA
  N3: J2.pulse, U4.D4
  N4: U4.D3, J1.pulse
  N5: U4.D5, J13.pin4
  N6: U4.D6, J13.pin3
  N7: U4.D7, J13.pin2
  N8: U4.D8, J13.pin1
  N9: J6.pin2, R2.Pin_0
  N10: Часть4.SIG, Часть6.AIN1
  N11: Часть6.AIN2, R2.Pin_1, R3.Pin_0
  N12: Часть6.AIN0, J8.pin2
  N13: S1.leg0, R9.Pin_0, R5.Pin_0
  N14: S1.leg1, S2.leg1, S3.leg1, S4.leg1, S5.leg1, J9.pin1
  N15: S2.leg0, R8.Pin_1, R6.Pin_0
  N16: S3.leg0, J9.pin2, R6.Pin_1, R7.Pin_1
  N17: S4.leg0, R5.Pin_1
  N18: S5.leg0, R9.Pin_1, R8.Pin_0
  N19: J9.pin3, R7.Pin_0
  N20: J4.pin1, U2.T2
  N21: J4.pin2, U2.T1
  VSS: LCD1.VSS, LCM1602_IIC1.VSS
  VDD: LCD1.VDD, LCM1602_IIC1.VDD
  N22: LCD1.V0, LCM1602_IIC1.V0
  N23: LCD1.RS, LCM1602_IIC1.RS
  N24: LCD1.R/W, LCM1602_IIC1.RW
  N25: LCD1.E, LCM1602_IIC1.E
  N26: LCD1.DB0, LCM1602_IIC1.D0
  N27: LCD1.DB1, LCM1602_IIC1.D1
  N28: LCD1.DB2, LCM1602_IIC1.D2
  N29: LCD1.DB3, LCM1602_IIC1.D3
  N30: LCD1.DB4, LCM1602_IIC1.D4
  N31: LCD1.DB5, LCM1602_IIC1.D5
  N32: LCD1.DB6, LCM1602_IIC1.D6
  N33: LCD1.DB7, LCM1602_IIC1.D7
  N34: LCD1.LED+, LCM1602_IIC1.A
  N35: LCD1.LED-, LCM1602_IIC1.K
  N36: U2.+, J12.pin4
  N37: U2.-, U3.-, J12.pin1, U1.-, U5.-
  N38: J10.pin1, LCM1602_IIC1.GND
  N39: J10.pin2, LCM1602_IIC1.VCC
  N40: J10.pin3, LCM1602_IIC1.SDA
  N41: J10.pin4, LCM1602_IIC1.SCL
  N42: J3.pin1, U3.T2
  N43: J3.pin2, U3.T1
  N44: U3.+, J12.pin3
  N45: LCM1602_IIC1.LED_A, LCM1602_IIC1.LED_B
  N46: J12.pin2, U5.+
  N47: J12.pin5, U1.+
  N48: J7.pin1, U5.T2
  N49: J7.pin2, U5.T1
  N50: J5.pin1, U1.T2
  N51: J5.pin2, U1.T1

custom parts:
  ESP8266 NodeMCU LoLin module: ESP8266 based NodeMCU
  Adafruit ADS1115 16Bit I2C ADC: For microcontrollers without an analog-to-digital converter or when you want a higher-precision ADC, the ADS1115 provides 16-bit precision at 860 samples/second over I2C. The chip can be configured as 4 single-ended input channels, or two differential channels. As a nice bonus, it even includes a programmable gain amplifier, up to x16, to help boost up smaller single/differential signals to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
  LCM1602 IIC: I2C-Module to use a 1602 or 2004 LCD on with the wire.h libory Serial LCD Modul
