# Fritzing sketch Схема (saved by Fritzing 0.9.3b)
breadboards: 1

parts:
  LCD1 = LCD screen
  Часть2 = Real Time Clock Module - DS1307 RTC Breakout Board
  Часть3 = BME280 Breakout
  J1 = Basic Servo
  J2 = Basic Servo
  LCM1602_IIC1 = LCM1602 IIC [part_number="LCM1602 IIC" chip_label="LCM1602 IIC" package="DIP (Dual Inline) [THT]"]
  U1 = RELAY-SOLIDSTATE [package=relay-s108t02]
  U2 = RELAY-SOLIDSTATE [package=relay-s108t02]
  U3 = RELAY-SOLIDSTATE [package=relay-s108t02]
  U4 = ESP8266 NodeMCU LoLin module
  J3 = Screw terminal - 2 pins [package=THT]
  J4 = Screw terminal - 2 pins [package=THT]
  J5 = Screw terminal - 2 pins [package=THT]
  R2 = Resistor [tolerance=±5% resistance=220 package="2512 [SMD]"]
  J6 = Screw terminal - 2 pins [package=THT]
  R3 = Resistor [tolerance=±5% resistance=220 package="2512 [SMD]"]
  Часть4 = Soil Moisture Sensor
  Часть6 = Adafruit ADS1115 16Bit I2C ADC [part_number="Adafruit #1085"]
  S1 = Round Pushbutton
  R4 = Resistor [tolerance=±5% resistance=220 package="2512 [SMD]"]  # not connected
  R5 = Resistor [tolerance=±5% resistance=220 package="2512 [SMD]"]
  S2 = Round Pushbutton
  R6 = Resistor [tolerance=±5% resistance=220 package="2512 [SMD]"]
  S3 = Round Pushbutton
  R7 = Resistor [tolerance=±5% resistance=220 package="2512 [SMD]"]
  S4 = Round Pushbutton
  R8 = Resistor [tolerance=±5% resistance=220 package="2512 [SMD]"]
  S5 = Round Pushbutton
  R9 = Resistor [tolerance=±5% resistance=220 package="2512 [SMD]"]

nets:
  VSS: LCD1.VSS, LCM1602_IIC1.VSS
  VDD: LCD1.VDD, LCM1602_IIC1.VDD
  N1: LCD1.V0, LCM1602_IIC1.V0
  N2: LCD1.RS, LCM1602_IIC1.RS
  N3: LCD1.R/W, LCM1602_IIC1.RW
  N4: LCD1.E, LCM1602_IIC1.E
  N5: LCD1.DB0, LCM1602_IIC1.D0
  N6: LCD1.DB1, LCM1602_IIC1.D1
  N7: LCD1.DB2, LCM1602_IIC1.D2
  N8: LCD1.DB3, LCM1602_IIC1.D3
  N9: LCD1.DB4, LCM1602_IIC1.D4
  N10: LCD1.DB5, LCM1602_IIC1.D5
  N11: LCD1.DB6, LCM1602_IIC1.D6
  N12: LCD1.DB7, LCM1602_IIC1.D7
  N13: LCD1.LED+, LCM1602_IIC1.A
  N14: LCD1.LED-, LCM1602_IIC1.K
  5V: Часть2.5V, Часть3.3.3V, J1.vcc, J2.vcc, LCM1602_IIC1.VCC, R3.Pin_1, Часть4.VCC, Часть6.VDD, R7.Pin_0
  GND: Часть2.GND, Часть3.GND, J1.gnd, J2.gnd, LCM1602_IIC1.GND, U1.-, U2.-, U3.-, U4.GND, J6.pin1, Часть4.GND, Часть6.SCL, Часть6.GND, S1.leg1, S2.leg1, S3.leg1, S4.leg1, S5.leg1
  N15: Часть2.SCL, Часть3.SCK/SCL, LCM1602_IIC1.SCL, U4.D1
  N16: Часть2.SDA, Часть3.SDI/SDA, LCM1602_IIC1.SDA, U4.D2
  N17: J1.pulse, U4.S2
  N18: J2.pulse, U4.S3
  N19: LCM1602_IIC1.LED_A, LCM1602_IIC1.LED_B
  N20: U1.T1, J5.pin2
  N21: U1.T2, J5.pin1
  N22: U1.+, U4.D5
  N23: U2.T1, J4.pin2
  N24: U2.T2, J4.pin1
  N25: U2.+, U4.D6
  N26: U3.T1, J3.pin2
  N27: U3.T2, J3.pin1
  N28: U3.+, U4.D7
  N29: U4.VU, Часть6.SDA
  N30: R2.Pin_0, J6.pin2
  N31: R2.Pin_1, R3.Pin_0, Часть6.AIN1
  N32: Часть4.SIG, Часть6.AIN0
  N33: Часть6.AIN2, R6.Pin_1, S3.leg0, R7.Pin_1
  N34: S1.leg0, R5.Pin_0, R9.Pin_0
  N35: R5.Pin_1, S4.leg0
  N36: S2.leg0, R6.Pin_0, R8.Pin_1
  N37: R8.Pin_0, S5.leg0, R9.Pin_1

custom parts:
  LCM1602 IIC: I2C-Module to use a 1602 or 2004 LCD on with the wire.h libory Serial LCD Modul
  ESP8266 NodeMCU LoLin module: ESP8266 based NodeMCU
  Adafruit ADS1115 16Bit I2C ADC: For microcontrollers without an analog-to-digital converter or when you want a higher-precision ADC, the ADS1115 provides 16-bit precision at 860 samples/second over I2C. The chip can be configured as 4 single-ended input channels, or two differential channels. As a nice bonus, it even includes a programmable gain amplifier, up to x16, to help boost up smaller single/differential signals to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
